# Fritzing sketch WiringDiagramFritzingFile (saved by Fritzing 0.9.6b)

parts:
  L298N1 = L298N DC motor driver
  Mod1 = Raspberry Pi 4B
  M2 = DC Motor
  M3 = DC Motor
  M4 = DC Motor
  M5 = DC Motor
  BAT2 = Battery Holders [package=battery-aaa]
  BAT3 = Battery Holders [package=battery-aaa]
  BAT4 = Battery Holders [package=battery-aaa]

nets:
  N1: L298N1.OUT1, M3.pin_1, M4.pin_1
  N2: L298N1.OUT2, M3.pin_2, M4.pin_2
  N3: L298N1.OUT3, M2.pin_1, M5.pin_1
  N4: L298N1.OUT4, M2.pin_2, M5.pin_2
  N5: L298N1.12V, BAT2.+, BAT3.+, BAT4.+
  GND: L298N1.GND, Mod1.GND, BAT2.-, BAT3.-, BAT4.-
  5V: L298N1.5V, Mod1.5V, Mod1.GPIO2

custom parts:
  L298N DC motor driver: 2x DC motor driver with 78M05 positive voltage regulator (7..35 V) L298N: max 46 V, 2 A Set 5 V Enable jumper to enable 5 V regultor (needed for the L298N) and +5 V output at screw terminal or supply external +5 V at screw terminal Set ENA and/or ENB to +5 V to enable motor permanently or supply ENA and/or ENB with PWM signal IN1 and IN2 set rotation directory for motor A (OUT1/OUT2) IN2 and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
